# Fritzing sketch Pulsador_Fritzing (saved by Fritzing 1.0.3b)
breadboards: 1

parts:
  Componente1 = Arduino Uno (Rev3)
  LED1 = LED - 5mm [color="Red (633nm)" current=0.030A package="5 mm [THT]"]
  R1 = Resistor [tolerance=±5% resistance=220 package="0603 [SMD]"]
  S1 = Momentary Switch [package=ksa_sealed_tac_switch]
  R2 = Resistor [tolerance=±5% power=0.25W resistance=220 package=THT]

nets:
  N1: Componente1.D13/SCK, LED1.anode
  N2: Componente1.GND, R1.Pin_0, R2.Pin_0
  N3: Componente1.D2, S1.3
  N4: Componente1.5V, S1.2
  N5: LED1.cathode, R1.Pin_1
  N6: S1.4, R2.Pin_1

// code stored in the sketch: Pulsador_Fritzing.ino

byte ledP = 13;
byte button = 2;

int buttonState = 0;


void setup()
{
  pinMode(ledP, OUTPUT);
  pinMode(button, INPUT);
}

void loop()
{
  
  buttonState = digitalRead(button);
  
  if(buttonState == HIGH){
    digitalWrite(ledP, HIGH);
  
  
  
  }
  
  else {
    digitalWrite(ledP,LOW);
  
  
  
  }
  
   delay(15);
}
